# Fritzing sketch DHT11_and_BMP180_Weather_Station (saved by Fritzing 0.9.3b)

parts:
  Arduino_UNO = Arduino Uno (Rev3)
  DHT11_Temperature_&_Humidity_Sensor = KY-015 Temperature & Humidity Sensor Module [package="Breakout board"]
  BMP180_Barometric_Pressure_Sensor = Barometric Pressure Sensor - BMP180 Breakout (GY-68)
  I2C_Level_Shifter = I2C level shifter bidirectional
  LCD2004-I2C_Display_Module = LCD2004-I2C

nets:
  GND: Arduino_UNO.GND, DHT11_Temperature_&_Humidity_Sensor.-, BMP180_Barometric_Pressure_Sensor.GND, I2C_Level_Shifter.GND, LCD2004-I2C_Display_Module.GND
  N1: Arduino_UNO.A4/SDA, I2C_Level_Shifter.HV1, LCD2004-I2C_Display_Module.SDA
  N2: Arduino_UNO.A5/SCL, I2C_Level_Shifter.HV2, LCD2004-I2C_Display_Module.SCL
  N3: Arduino_UNO.D4, DHT11_Temperature_&_Humidity_Sensor.S
  3V3: Arduino_UNO.3V3, BMP180_Barometric_Pressure_Sensor.VCC, I2C_Level_Shifter.LV
  5V: Arduino_UNO.5V, DHT11_Temperature_&_Humidity_Sensor.Vin, I2C_Level_Shifter.HV, LCD2004-I2C_Display_Module.VCC
  N4: BMP180_Barometric_Pressure_Sensor.SCL, I2C_Level_Shifter.LV2
  N5: BMP180_Barometric_Pressure_Sensor.SDA, I2C_Level_Shifter.LV1

notes:
  DHT11_and_BMP180_Weather_Station

custom parts:
  KY-015 Temperature & Humidity Sensor Module: KY-015 temperature and humidity sensor module, provides a low-latency serial interface to measure humidity and temperature.
  LCD2004-I2C: A standard character display with 4x20 characters. Comes in many colors with LCM2004 IIC attached.

// code stored in the sketch: I2C_Serial_Interface_1602_LCD_Module._Test.ino
#include <Wire.h> 
#include <LiquidCrystal_I2C.h>       // Include library
//#include <LiquidCrystal_PCF8574.h> // Include alternative library if necessary

LiquidCrystal_I2C lcd(0x27,16,2);    // Set I2C address (common value), and screen parameters (for LCD 1602 - 2 lines 16 symbol each 
//LiquidCrystal_PCF8574 lcd(0x27);   // Variant for the PCF8574 library

void setup()
{
  lcd.init();                        // Init display  
  lcd.backlight();                   // Turn backlite on
  lcd.setCursor(0,0);                // Set cursor at the beginning of the first line
  lcd.print("Hello Yulia!");         // Print the first line
  lcd.setCursor(0,1);                // Set cursor at the beginning of the second line
  lcd.print("How are you?");         // Print the second line
}
void loop()
{
}

// code stored in the sketch: Project_30_-_DHT11_Temperature_and_Humidity_Sensor.ino
// Project 30: DHT11 Temperature and Humidity Sensor
////////////////////////////////
#include <Wire.h> 
#include <LiquidCrystal_I2C.h>       // Include library
//#include <LiquidCrystal_PCF8574.h> // Include alternative library if necessary
#include <dht11.h>

LiquidCrystal_I2C lcd(0x27,16,2);    // Set I2C address (common value), and screen parameters (for LCD 1602 - 2 lines 16 symbol each 
//LiquidCrystal_PCF8574 lcd(0x27);   // Variant for the PCF8574 library

dht11 DHT;
#define DHT11_PIN 4

void setup()
{
  lcd.init();                        // Init display  
  lcd.backlight();                   // Turn backlite on
  
  Serial.begin(9600);
  Serial.println("DHT TEST PROGRAM ");
  Serial.print("LIBRARY VERSION: ");
  Serial.println(DHT11LIB_VERSION);
  Serial.println();
  Serial.println("Type,\tstatus,\tHumidity (%),\tTemperature (C)");
}
void loop()
{
  int chk;
  Serial.print("DHT11, \t");
  chk = DHT.read(DHT11_PIN);    // READ DATA
  switch (chk){
    case DHTLIB_OK:  
                Serial.print("OK,\t"); 
                break;

case DHTLIB_ERROR_CHECKSUM: 

                Serial.print("Checksum error,\t"); 
                break;
    case DHTLIB_ERROR_TIMEOUT: 
                Serial.print("Time out error,\t"); 
                break;
    default: 
                Serial.print("Unknown error,\t"); 
                break;
  }
 // DISPLAY DATA
  Serial.print(DHT.humidity,1);
  Serial.print(",\t");
  Serial.println(DHT.temperature,1);
  //lcd.clear();
  lcd.setCursor(0, 0);
  lcd.print("TEMPERATURE: ");
  lcd.print(DHT.temperature);
  lcd.print("C ");
  lcd.setCursor(0, 1);
  lcd.print("HUMIDITY: ");
  lcd.print(DHT.humidity);
  lcd.print("%");
  delay(2000);
}
